# Fritzing sketch Esquema Arduino Editavel (saved by Fritzing 0.9.2b)
breadboards: 1

parts:
  Componente1 = Arduino Uno (Rev3) - ICSP
  U1 = LCD-16X2 [package=lcd-16x2]
  RTC = Real Time Clock Module - DS1307 RTC Breakout Board
  RFID = RFID USB Reader
  U2 = POT [package=pot_alpha_rv16af-20]
  LED1 = smd LED [color="Red (633nm)" package="0805 [SMD]"]
  R1 = Resistor [tolerance=±5% resistance=220 package="0603 [SMD]"]
  J1 = Piezo Speaker

nets:
  N1: Componente1.A4/SDA, RTC.SQW
  N2: Componente1.A5/SCL, RTC.SCL
  N3: Componente1.D8, R1.Pin_1
  N4: Componente1.D9_PWM, RFID.GND
  N5: Componente1.D10_PWM/SS, RFID.GNDT
  N6: Componente1.D11_PWM/MOSI, RFID.ANT2
  N7: Componente1.D12/MISO, RFID.ANT1
  N8: Componente1.D13/SCK, RFID.CP
  N9: Componente1.D2, U1.DB7
  N10: Componente1.D3_PWM, U1.DB6
  N11: Componente1.D4, U1.DB5
  N12: Componente1.D5_PWM, U1.DB4
  N13: Componente1.D6_PWM, U1.RS
  N14: Componente1.D7, U1.E
  3V3: Componente1.3V3, RFID.VCC
  5V: Componente1.5V, U1.VDD, U1.A, RTC.5V, U2.E
  GND: Componente1.GND, U1.VSS, U1.R_W, U1.K, RTC.GND, RFID.TX-O, U2.A, LED1.cathode, J1.pin2
  N15: U1.VO, U2.S
  N16: LED1.anode, R1.Pin_0, J1.pin1
